# Fritzing sketch Breadboard (saved by Fritzing 0.9.4)
breadboards: 1

parts:
  Part1 = Arduino Uno (Rev3) - ICSP
  Part2 = BME280 Breakout
  Part3 = LCD1602-I2C
  J4 = female pin header, 4 pins [form="♀ (female)"]
  J3 = female pin header, 4 pins [form="♀ (female)"]
  U2 = ESP8266 WiFi Module [part_number=ESP8266]
  R1 = Resistor [tolerance=±5% resistance=220 package=THT]
  R2 = Resistor [tolerance=±5% resistance=220 package=THT]
  R3 = Resistor [tolerance=±5% resistance=220 package=THT]

nets:
  N1: Part1.A4/SDA, Part2.SDI/SDA, Part3.SDA, J4.pin1, J3.pin1
  N2: Part1.A5/SCL, Part2.SCK/SCL, Part3.SCL, J4.pin2, J3.pin2
  N3: Part1.D6_PWM, U2.TXD
  N4: Part1.D7, R3.Pin_1
  3V3: Part1.3V3, U2.VCC, U2.CH_PD
  5V: Part1.5V, Part2.3.3V, Part3.VCC, J4.pin3, J3.pin3
  GND: Part1.GND, Part2.GND, Part3.GND, J4.pin4, J3.pin4, U2.GND, R1.Pin_0
  N5: U2.RXD, R2.Pin_1, R3.Pin_0
  N6: R1.Pin_1, R2.Pin_0

custom parts:
  LCD1602-I2C: A standard character display, usually with 2x16 characters. Comes in many colors with LCM1602 IIC attached.
  ESP8266 WiFi Module: Generic WiFi Module based on the ESP8266 with onboard PCB antenna and UART communications
